// Logisim project main.circ as structural Verilog: 3 circuits, main circuit main
module main (
  input  in_1,
  input  in_2,
  output out_3,
  output out_4,
  output out_5,
  output out_6,
  output out_7,
  output out_8,
  output out_9,
  output out_10,
  output out_11,
  output out_12,
  output out_13,
  output out_14,
  output out_15,
  output out_16,
  output out_17,
  output out_18,
  output out_19,
  output out_20,
  output out_21,
  output out_22,
  output out_23,
  output out_24,
  output out_25,
  output out_26,
  output out_27
);

  wire C;
  wire [31:0] undriven, undriven_2;

  Clock clock_1 (.out(C));
  \cell  cell_1 (
    .in_4(in_1), .clock(C), .in_5(out_4), .in_1(in_1), .in_2(in_1), .in_3(in_1), .in_7(in_1), .in_8(out_8),
    .in_9(out_9), .state(out_3));
  \cell  cell_2 (
    .in_4(in_1), .clock(C), .in_5(out_9), .in_1(in_1), .in_2(out_3), .in_3(out_4), .in_7(in_1),
    .in_8(out_13), .in_9(out_14), .state(out_8));
  \cell  cell_3 (
    .in_4(in_1), .clock(C), .in_5(out_14), .in_1(in_1), .in_2(out_8), .in_3(out_9), .in_7(in_1),
    .in_8(out_18), .in_9(out_19), .state(out_13));
  \cell  cell_4 (
    .in_4(in_1), .clock(C), .in_5(out_19), .in_1(in_1), .in_2(out_13), .in_3(out_14), .in_7(in_1),
    .in_8(out_23), .in_9(out_24), .state(out_18));
  \cell  cell_5 (
    .in_4(in_1), .clock(C), .in_5(out_24), .in_1(in_1), .in_2(out_18), .in_3(out_19), .in_7(in_2),
    .in_8(in_2), .in_9(in_2), .state(out_23));
  \cell  cell_6 (
    .in_4(out_3), .clock(C), .in_5(out_5), .in_1(in_1), .in_2(in_1), .in_3(in_1), .in_7(out_8), .in_8(out_9),
    .in_9(out_10), .state(out_4));
  \cell  cell_7 (
    .in_4(out_8), .clock(C), .in_5(out_10), .in_1(out_3), .in_2(out_4), .in_3(out_5), .in_7(out_13),
    .in_8(out_14), .in_9(out_15), .state(out_9));
  \cell  cell_8 (
    .in_4(out_13), .clock(C), .in_5(out_15), .in_1(out_8), .in_2(out_9), .in_3(out_10), .in_7(out_18),
    .in_8(out_19), .in_9(out_20), .state(out_14));
  \cell  cell_9 (
    .in_4(out_18), .clock(C), .in_5(out_20), .in_1(out_13), .in_2(out_14), .in_3(out_15), .in_7(out_23),
    .in_8(out_24), .in_9(out_25), .state(out_19));
  \cell  cell_10 (
    .in_4(out_23), .clock(C), .in_5(out_25), .in_1(out_18), .in_2(out_19), .in_3(out_20), .in_7(in_2),
    .in_8(in_2), .in_9(in_2), .state(out_24));
  \cell  cell_11 (
    .in_4(out_4), .clock(C), .in_5(out_6), .in_1(in_1), .in_2(in_1), .in_3(in_1), .in_7(out_9),
    .in_8(out_10), .in_9(out_11), .state(out_5));
  \cell  cell_12 (
    .in_4(out_9), .clock(C), .in_5(out_11), .in_1(out_4), .in_2(out_5), .in_3(out_6), .in_7(out_14),
    .in_8(out_15), .in_9(out_16), .state(out_10));
  \cell  cell_13 (
    .in_4(out_14), .clock(C), .in_5(out_16), .in_1(out_9), .in_2(out_10), .in_3(out_11), .in_7(out_19),
    .in_8(out_20), .in_9(out_21), .state(out_15));
  \cell  cell_14 (
    .in_4(out_19), .clock(C), .in_5(out_21), .in_1(out_14), .in_2(out_15), .in_3(out_16), .in_7(out_24),
    .in_8(out_25), .in_9(out_26), .state(out_20));
  \cell  cell_15 (
    .in_4(out_24), .clock(C), .in_5(out_26), .in_1(out_19), .in_2(out_20), .in_3(out_21), .in_7(in_2),
    .in_8(in_2), .in_9(in_2), .state(out_25));
  \cell  cell_16 (
    .in_4(out_5), .clock(C), .in_5(out_7), .in_1(in_1), .in_2(in_1), .in_3(in_1), .in_7(out_10),
    .in_8(out_11), .in_9(out_12), .state(out_6));
  \cell  cell_17 (
    .in_4(out_10), .clock(C), .in_5(out_12), .in_1(out_5), .in_2(out_6), .in_3(out_7), .in_7(out_15),
    .in_8(out_16), .in_9(out_17), .state(out_11));
  \cell  cell_18 (
    .in_4(out_15), .clock(C), .in_5(out_17), .in_1(out_10), .in_2(out_11), .in_3(out_12), .in_7(out_20),
    .in_8(out_21), .in_9(out_22), .state(out_16));
  \cell  cell_19 (
    .in_4(out_20), .clock(C), .in_5(out_22), .in_1(out_15), .in_2(out_16), .in_3(out_17), .in_7(out_25),
    .in_8(out_26), .in_9(out_27), .state(out_21));
  \cell  cell_20 (
    .in_4(out_25), .clock(C), .in_5(out_27), .in_1(out_20), .in_2(out_21), .in_3(out_22), .in_7(in_2),
    .in_8(in_2), .in_9(in_2), .state(out_26));
  \cell  cell_21 (
    .in_4(out_6), .clock(C), .in_5(in_1), .in_1(in_1), .in_2(in_1), .in_3(in_1), .in_7(out_11),
    .in_8(out_12), .in_9(in_1), .state(out_7));
  \cell  cell_22 (
    .in_4(out_11), .clock(C), .in_5(in_1), .in_1(out_6), .in_2(out_7), .in_3(in_1), .in_7(out_16),
    .in_8(out_17), .in_9(in_1), .state(out_12));
  \cell  cell_23 (
    .in_4(out_16), .clock(C), .in_5(in_1), .in_1(out_11), .in_2(out_12), .in_3(in_1), .in_7(out_21),
    .in_8(out_22), .in_9(in_1), .state(out_17));
  \cell  cell_24 (
    .in_4(out_21), .clock(C), .in_5(in_1), .in_1(out_16), .in_2(out_17), .in_3(in_1), .in_7(out_26),
    .in_8(out_27), .in_9(in_1), .state(out_22));
  \cell  cell_25 (
    .in_4(out_26), .clock(C), .in_5(in_1), .in_1(out_21), .in_2(out_22), .in_3(in_1), .in_7(in_2),
    .in_8(in_2), .in_9(in_2), .state(out_27));
  DotMatrix #(.matrixcols(32), .matrixrows(32)) dotmatrix_1 (
    .col0(undriven), .col1(undriven_2));  // open: col2, col3, col4, col5, col6, col7, col8, col9, col10, col11, col12, col13, col14, col15, col16, col17, col18, col19, col20, col21, col22, col23, col24, col25, col26, col27, col28, col29, col30, col31
endmodule

module breeding (
  input  in_1,
  input  in_2,
  input  in_3,
  input  in_4,
  input  in_5,
  input  in_6,
  input  in_7,
  input  in_8,
  input  in_9,
  output out_10
);

  wire and_1_out, comparator_1_eq, comparator_2_eq;
  wire [3:0] bitadder_1_out;

  BitAdder bitadder_1 (.in0({in_8, in_7, in_6, in_5, in_4, in_3, in_2, in_1}), .out(bitadder_1_out));
  Comparator #(.width(4), .mode("unsigned")) comparator_1 (
    .a(bitadder_1_out), .b(4'b0011), .eq(comparator_1_eq));  // open: gt, lt
  Comparator #(.width(4), .mode("unsigned")) comparator_2 (
    .a(bitadder_1_out), .b(4'b0010), .eq(comparator_2_eq));  // open: gt, lt
  and and_1 (and_1_out, comparator_2_eq, in_9);
  or or_1 (out_10, comparator_1_eq, and_1_out);

  // Notes on the sheet:
  //   Neighbours
  //   Alive?
  //   Alive?
endmodule

module \cell  (
  input  in_1,
  input  in_2,
  input  in_3,
  input  in_4,
  input  in_5,
  input  clock,
  input  in_7,
  input  in_8,
  input  in_9,
  output state
);

  wire breeding_1_out_10;

  breeding breeding_1 (
    .in_1(in_3), .in_2(in_2), .in_3(in_1), .in_4(in_4), .in_5(in_5), .in_6(in_7), .in_7(in_8), .in_8(in_9),
    .in_9(state), .out_10(breeding_1_out_10));
  D_Flip_Flop d_ff_1 (.clk(clock), .D(breeding_1_out_10), .Q(state));  // open: Qn, preset, en, reset
endmodule
